// Logisim project 8086.circ as structural Verilog: 1 circuit, main circuit main
module main (
  input  CLK,
  input  [31:0] Instruction_Code,
  output [15:0] out_3
);

  wire and_1_out, decoder_2_out0, decoder_2_out1, decoder_3_out0, decoder_3_out1, decoder_3_out2,
       decoder_3_out3, decoder_3_out4, decoder_3_out5, decoder_3_out6, decoder_3_out7, decoder_4_out0,
       decoder_4_out1, decoder_4_out2, decoder_4_out3, decoder_4_out4, decoder_4_out5, decoder_4_out6,
       decoder_4_out7, Immediate_to_Register_out, not_1_out, or_1_out, or_2_out, or_6_out, or_7_out,
       or_8_out, or_9_out, or_10_out, or_11_out, or_12_out, or_13_out, RegisterMemory_ToFrom_Register_out;
  wire [2:0] multiplexer_1_out, multiplexer_2_out, or_3_out;
  wire [7:0] AH_q, AL_q, BH_q, BL_q, CH_q, CL_q, DH_q, DL_q, multiplexer_3_out, multiplexer_4_out,
       multiplexer_5_out, multiplexer_6_out, multiplexer_7_out, pull_resistor_1_node, pull_resistor_2_node;
  wire [15:0] BasePointer_q, demultiplexer_1_out1, DestinationIndex_q, multiplexer_8_out, or_5_out,
       or_14_out, SourceIndex_q, StackPointer_q;

  and RegisterMemory_ToFrom_Register (RegisterMemory_ToFrom_Register_out, ~Instruction_Code[26], Instruction_Code[27], ~Instruction_Code[28], ~Instruction_Code[29], ~Instruction_Code[30], Instruction_Code[31]);  // AND_Gate
  and Immediate_to_Register (Immediate_to_Register_out, Instruction_Code[28], Instruction_Code[29], ~Instruction_Code[30], Instruction_Code[31]);  // AND_Gate
  not not_1 (not_1_out, Instruction_Code[25]);
  Multiplexer #(.width(3)) multiplexer_1 (
    .in0(Instruction_Code[18:16]), .in1(Instruction_Code[21:19]), .out(multiplexer_1_out),
    .sel(Instruction_Code[25]), .en(RegisterMemory_ToFrom_Register_out));
  Decoder #(.select(2)) decoder_1 (
    .sel(Instruction_Code[23:22]), .en(RegisterMemory_ToFrom_Register_out));  // open: out0, out1, out2, out3
  Multiplexer #(.width(3)) multiplexer_2 (
    .in0(Instruction_Code[18:16]), .in1(Instruction_Code[21:19]), .out(multiplexer_2_out), .sel(not_1_out),
    .en(RegisterMemory_ToFrom_Register_out));
  and and_1 (and_1_out, Instruction_Code[24], RegisterMemory_ToFrom_Register_out);
  Pull_Resistor pull_resistor_1 (.node(pull_resistor_1_node));
  assign pull_resistor_1_node = Immediate_to_Register_out ? Instruction_Code[15:8] : 8'bz;  // Controlled_Buffer controlled_buffer_1
  Pull_Resistor pull_resistor_2 (.node(pull_resistor_2_node));
  assign pull_resistor_2_node = Immediate_to_Register_out ? Instruction_Code[23:16] : 8'bz;  // Controlled_Buffer controlled_buffer_2
  // Probe on multiplexer_2_out
  // Probe on RegisterMemory_ToFrom_Register_out
  or or_1 (or_1_out, RegisterMemory_ToFrom_Register_out, Immediate_to_Register_out);
  or or_2 (or_2_out, Instruction_Code[27], and_1_out);
  // Probe on or_2_out
  // Probe on or_1_out
  Decoder decoder_2 (.out0(decoder_2_out0), .out1(decoder_2_out1), .sel(or_2_out), .en(or_1_out));
  // AND_Gate and_2 is placed but not wired
  // Probe on or_3_out
  assign or_3_out = multiplexer_1_out | Instruction_Code[26:24];  // OR_Gate or_3, 3 bits wide
  Decoder #(.select(3)) decoder_3 (
    .out0(decoder_3_out0), .out1(decoder_3_out1), .out2(decoder_3_out2), .out3(decoder_3_out3),
    .out4(decoder_3_out4), .out5(decoder_3_out5), .out6(decoder_3_out6), .out7(decoder_3_out7),
    .sel(or_3_out), .en(decoder_2_out0));
  Decoder #(.select(3)) decoder_4 (
    .out0(decoder_4_out0), .out1(decoder_4_out1), .out2(decoder_4_out2), .out3(decoder_4_out3),
    .out4(decoder_4_out4), .out5(decoder_4_out5), .out6(decoder_4_out6), .out7(decoder_4_out7),
    .sel(or_3_out), .en(decoder_2_out1));
  // Probe on pull_resistor_1_node
  // Probe on pull_resistor_2_node
  assign or_5_out[15:8] = demultiplexer_1_out1[15:8] | pull_resistor_1_node;  // OR_Gate or_4, 8 bits wide
  assign or_5_out[7:0] = demultiplexer_1_out1[7:0] | pull_resistor_2_node;  // OR_Gate or_5, 8 bits wide
  or or_6 (or_6_out, decoder_3_out0, decoder_4_out0);
  or or_7 (or_7_out, decoder_3_out1, decoder_4_out1);
  or or_8 (or_8_out, decoder_3_out2, decoder_4_out2);
  or or_9 (or_9_out, decoder_3_out3, decoder_4_out3);
  or or_10 (or_10_out, decoder_3_out4, decoder_4_out0);
  or or_11 (or_11_out, decoder_3_out5, decoder_4_out1);
  or or_12 (or_12_out, decoder_3_out6, decoder_4_out2);
  or or_13 (or_13_out, decoder_3_out7, decoder_4_out3);
  Register AL (.D(or_5_out[7:0]), .en(or_6_out), .clk(CLK), .Q(AL_q));  // open: clr
  Register CL (.D(or_5_out[7:0]), .en(or_7_out), .clk(CLK), .Q(CL_q));  // open: clr
  Register DL (.D(or_5_out[7:0]), .en(or_8_out), .clk(CLK), .Q(DL_q));  // open: clr
  Register BL (.D(or_5_out[7:0]), .en(or_9_out), .clk(CLK), .Q(BL_q));  // open: clr
  Register AH (.D(multiplexer_3_out), .en(or_10_out), .clk(CLK), .Q(AH_q));  // open: clr
  Multiplexer #(.enable("false"), .width(8)) multiplexer_3 (
    .in0(or_5_out[7:0]), .in1(or_5_out[15:8]), .out(multiplexer_3_out), .sel(decoder_2_out1));
  Register CH (.D(multiplexer_4_out), .en(or_11_out), .clk(CLK), .Q(CH_q));  // open: clr
  Multiplexer #(.enable("false"), .width(8)) multiplexer_4 (
    .in0(or_5_out[7:0]), .in1(or_5_out[15:8]), .out(multiplexer_4_out), .sel(decoder_2_out1));
  Register DH (.D(multiplexer_5_out), .en(or_12_out), .clk(CLK), .Q(DH_q));  // open: clr
  Multiplexer #(.enable("false"), .width(8)) multiplexer_5 (
    .in0(or_5_out[7:0]), .in1(or_5_out[15:8]), .out(multiplexer_5_out), .sel(decoder_2_out1));
  Register BH (.D(multiplexer_6_out), .en(or_13_out), .clk(CLK), .Q(BH_q));  // open: clr
  Multiplexer #(.enable("false"), .width(8)) multiplexer_6 (
    .in0(or_5_out[7:0]), .in1(or_5_out[15:8]), .out(multiplexer_6_out), .sel(decoder_2_out1));
  Register #(.width(16)) StackPointer (.D(or_5_out), .en(decoder_4_out4), .clk(CLK), .Q(StackPointer_q));  // open: clr
  Register #(.width(16)) BasePointer (.D(or_5_out), .en(decoder_4_out5), .clk(CLK), .Q(BasePointer_q));  // open: clr
  Register #(.width(16)) SourceIndex (.D(or_5_out), .en(decoder_4_out6), .clk(CLK), .Q(SourceIndex_q));  // open: clr
  Register #(.width(16)) DestinationIndex (
    .D(or_5_out), .en(decoder_4_out7), .clk(CLK), .Q(DestinationIndex_q));  // open: clr
  Multiplexer #(.enable("false"), .select(3), .width(8)) multiplexer_7 (
    .in0(AL_q), .in1(CL_q), .in2(DL_q), .in3(BL_q), .in4(AH_q), .in5(CH_q), .in6(DH_q), .in7(BH_q),
    .out(multiplexer_7_out), .sel(multiplexer_2_out));
  Multiplexer #(.enable("false"), .select(3), .width(16)) multiplexer_8 (
    .in0({AH_q, AL_q}), .in1({CH_q, CL_q}), .in2({DH_q, DL_q}), .in3({BH_q, BL_q}), .in4(StackPointer_q),
    .in5(BasePointer_q), .in6(SourceIndex_q), .in7(DestinationIndex_q), .out(multiplexer_8_out),
    .sel(multiplexer_2_out));
  // Probe on demultiplexer_1_out1
  assign or_14_out = {{8{1'b0}}, multiplexer_7_out} | multiplexer_8_out;  // OR_Gate or_14, 16 bits wide
  Demultiplexer #(.enable("false"), .width(16)) demultiplexer_1 (
    .out0(out_3), .out1(demultiplexer_1_out1), .in(or_14_out), .sel(RegisterMemory_ToFrom_Register_out));
endmodule
