// Logisim project lil_CPU.circ as structural Verilog: 13 circuits, main circuit main
module main (
  input  [15:0] in_1,
  input  [15:0] in_2,
  input  in_3
);

  wire clock_1_out, cpu_1_read_data_from_memory, cpu_1_write_data_to_memory;
  wire [15:0] cpu_1_instruction_pointer, cpu_1_main_bus_out, pull_resistor_1_node, ram_1_dout;
  wire [16:0] cpu_1_adress_bus_out;
  wire [31:0] rom_1_data;

  Clock clock_1 (.out(clock_1_out));
  // Probe on in_1
  // Probe on in_2
  CPU cpu_1 (
    .Write_Data_to_Memory(cpu_1_write_data_to_memory), .Read_Data_from_Memory(cpu_1_read_data_from_memory),
    .Main_Bus_Out(cpu_1_main_bus_out), .Instruction_Pointer(cpu_1_instruction_pointer),
    .Adress_Bus_Out(cpu_1_adress_bus_out), .RESET(in_3), .CLK(clock_1_out), .Instruction_Set(rom_1_data),
    .Main_Bus_In(pull_resistor_1_node));  // open: READ_IO, Write_IO
  // Probe on cpu_1_adress_bus_out
  RAM #(.addrWidth(17), .clearpin("true"), .dataWidth(16), .enables("line")) ram_1 (
    .addr(cpu_1_adress_bus_out), .we(cpu_1_write_data_to_memory), .clk(clock_1_out),
    .din(cpu_1_main_bus_out), .dout(ram_1_dout), .clr(in_3));
  // Probe on cpu_1_main_bus_out
  Pull_Resistor pull_resistor_1 (.node(pull_resistor_1_node));
  assign pull_resistor_1_node = cpu_1_read_data_from_memory ? ram_1_dout : 16'bz;  // Controlled_Buffer controlled_buffer_1
  ROM #(.addrWidth(16), .dataWidth(32)) rom_1 (.addr(cpu_1_instruction_pointer), .data(rom_1_data));

  // Notes on the sheet:
  //   contents of rom_1 (hex, n*v repeats v):
  //   1802a11 3800001 3c10001 4000000 4050000 5020000
endmodule

module CPU (
  input  [15:0] Main_Bus_In,
  input  RESET,
  input  CLK,
  input  [31:0] Instruction_Set,
  output [15:0] Main_Bus_Out,
  output [16:0] Adress_Bus_Out,
  output Write_Data_to_Memory,
  output Read_Data_from_Memory,
  output READ_IO,
  output Write_IO,
  output [15:0] Instruction_Pointer
);

  wire instruction_decoder_1_alu_enable, instruction_decoder_1_cache_select,
       instruction_decoder_1_immediate_address_enable, instruction_decoder_1_pop, instruction_decoder_1_push,
       instruction_decoder_1_reg_enable, instruction_decoder_1_reg_out_enable,
       instruction_decoder_1_reg_out_to_mainbus_select, instruction_decoder_1_word_select;
  wire [1:0] instruction_decoder_1_alu_a_in_select, instruction_decoder_1_alu_b_in_select,
       instruction_decoder_1_register_in_select;
  wire [2:0] instruction_decoder_1_reg_a_select, instruction_decoder_1_reg_b_select,
       instruction_decoder_1_reg_out_select, instruction_decoder_1_reg_select;
  wire [15:0] general_purpose_registers_1_a_out, general_purpose_registers_1_b_out,
       general_purpose_registers_1_to_internal_data_bus, general_purpose_registers_1_to_main_bus,
       relocation_registers_1_to_main_bus;

  // Probe on Instruction_Set
  assign Main_Bus_Out = relocation_registers_1_to_main_bus | general_purpose_registers_1_to_main_bus;  // OR_Gate or_1, 16 bits wide
  General_Purpose_Registers general_purpose_registers_1 (
    .A_Out(general_purpose_registers_1_a_out), .B_Out(general_purpose_registers_1_b_out),
    .To_Internal_Data_Bus(general_purpose_registers_1_to_internal_data_bus),
    .To_Main_Bus(general_purpose_registers_1_to_main_bus),
    .Register_in_Select(instruction_decoder_1_register_in_select),
    .REG_Out_to_Mainbus_Select(instruction_decoder_1_reg_out_to_mainbus_select), .From_Main_Bus(Main_Bus_In),
    .From_Internal_Data_Bus(general_purpose_registers_1_to_internal_data_bus),
    .Reg_Out_Select(instruction_decoder_1_reg_out_select), .REG_A_Select(instruction_decoder_1_reg_a_select),
    .REG_B_Select(instruction_decoder_1_reg_b_select), .REG_Select(instruction_decoder_1_reg_select),
    .Word_Select(instruction_decoder_1_word_select), .REG_Enable(instruction_decoder_1_reg_enable),
    .Cache_Select(instruction_decoder_1_cache_select), .Reset(RESET), .CLK(CLK),
    .Reg_Out_Enable(instruction_decoder_1_reg_out_enable));
  ALU alu_1 (
    .To_Internal_Bus(general_purpose_registers_1_to_internal_data_bus), .Instruction_Set(Instruction_Set),
    .B_IN(general_purpose_registers_1_b_out), .A_IN(general_purpose_registers_1_a_out),
    .ALU_A_IN_Select(instruction_decoder_1_alu_a_in_select),
    .ALU_B_IN_Select(instruction_decoder_1_alu_b_in_select),
    .From_Internal_Bus(general_purpose_registers_1_to_internal_data_bus),
    .ALU_Select(instruction_decoder_1_alu_enable), .CLK(CLK));
  Relocation_Registers relocation_registers_1 (
    .out_18(Instruction_Pointer), .To_Adress_Bus(Adress_Bus_Out[15:0]),
    .To_Internal_Data_Bus(general_purpose_registers_1_to_internal_data_bus),
    .To_Main_Bus(relocation_registers_1_to_main_bus), .A_Out(general_purpose_registers_1_a_out),
    .B_Out(general_purpose_registers_1_b_out), .POP(instruction_decoder_1_pop),
    .PUSH(instruction_decoder_1_push), .CLK(CLK), .RESET(RESET),
    .Word_Select(instruction_decoder_1_word_select), .REG_Enable(instruction_decoder_1_reg_enable),
    .REG_Select(instruction_decoder_1_reg_select),
    .Register_in_Select(instruction_decoder_1_register_in_select),
    .Reg_Out_Select(instruction_decoder_1_reg_out_select),
    .Reg_Out_Enable(instruction_decoder_1_reg_out_enable), .Cache_Select(instruction_decoder_1_cache_select),
    .REG_Out_to_Mainbus_Select(instruction_decoder_1_reg_out_to_mainbus_select),
    .Immediate_Address_Enable(instruction_decoder_1_immediate_address_enable),
    .REG_B_Select(instruction_decoder_1_reg_b_select), .REG_A_Select(instruction_decoder_1_reg_a_select),
    .From_Main_Bus(Main_Bus_In), .From_Internal_Data_Bus(general_purpose_registers_1_to_internal_data_bus));
  Instruction_Decoder instruction_decoder_1 (
    .REG_Enable(instruction_decoder_1_reg_enable), .REG_Select(instruction_decoder_1_reg_select),
    .Register_in_Select(instruction_decoder_1_register_in_select),
    .Reg_Out_Enable(instruction_decoder_1_reg_out_enable), .Read_Data_from_Memory(Read_Data_from_Memory),
    .Reg_Out_Select(instruction_decoder_1_reg_out_select), .Cache_Select(instruction_decoder_1_cache_select),
    .REG_Out_to_Mainbus_Select(instruction_decoder_1_reg_out_to_mainbus_select),
    .POP(instruction_decoder_1_pop), .PUSH(instruction_decoder_1_push),
    .To_Internal_Bus(general_purpose_registers_1_to_internal_data_bus),
    .Immediate_Address_Enable(instruction_decoder_1_immediate_address_enable),
    .ALU_Enable(instruction_decoder_1_alu_enable), .REG_A_Select(instruction_decoder_1_reg_a_select),
    .Write_Data_to_Memory(Write_Data_to_Memory), .REG_B_Select(instruction_decoder_1_reg_b_select),
    .ALU_A_IN_Select(instruction_decoder_1_alu_a_in_select),
    .ALU_B_IN_Select(instruction_decoder_1_alu_b_in_select), .Use_Cache(Adress_Bus_Out[16]),
    .Word_Select(instruction_decoder_1_word_select), .Instruction_Set(Instruction_Set));
endmodule

module Relocation_Registers (
  input  [2:0] REG_A_Select,
  input  [2:0] REG_B_Select,
  input  CLK,
  input  RESET,
  input  Immediate_Address_Enable,
  input  POP,
  input  PUSH,
  input  [15:0] From_Main_Bus,
  input  [15:0] From_Internal_Data_Bus,
  input  Word_Select,
  input  REG_Enable,
  input  [2:0] REG_Select,
  input  [1:0] Register_in_Select,
  input  [2:0] Reg_Out_Select,
  input  Reg_Out_Enable,
  input  Cache_Select,
  input  REG_Out_to_Mainbus_Select,
  output [15:0] out_18,
  output [15:0] A_Out,
  output [15:0] B_Out,
  output [15:0] To_Internal_Data_Bus,
  output [15:0] To_Main_Bus,
  output [15:0] To_Adress_Bus
);

  wire and_1_out, and_2_out, and_3_out, decoder_1_out4, decoder_1_out5, decoder_1_out6, not_1_out,
       one_bit_narrow_and_1_o, one_bit_narrow_or_1_o;
  wire [15:0] Base_Pointer_q, demultiplexer_1_out0, multiplexer_1_out, multiplexer_2_out, multiplexer_3_out,
       multiplexer_5_out, multiplexer_6_out, stack_pointer_1_data_out;

  Decoder #(.select(3)) decoder_1 (
    .out4(decoder_1_out4), .out5(decoder_1_out5), .out6(decoder_1_out6), .sel(REG_Select), .en(and_1_out));  // open: out0, out1, out2, out3, out7
  and and_1 (and_1_out, Word_Select, REG_Enable);
  and and_2 (and_2_out, Word_Select, Reg_Out_Enable);
  not not_1 (not_1_out, POP);
  One_Bit_Narrow_OR one_bit_narrow_or_1 (.O(one_bit_narrow_or_1_o), .A(POP), .B(PUSH));
  Multiplexer #(.enable("false"), .select(2), .width(16)) multiplexer_1 (
    .in0(multiplexer_2_out), .in1(From_Internal_Data_Bus), .in2(From_Main_Bus), .out(multiplexer_1_out),
    .sel(Register_in_Select));  // open: in3
  Counter #(.max('hffff), .trigger("falling"), .width(16)) Instruction_Pointer (
    .load(decoder_1_out6), .D(multiplexer_1_out), .Q(out_18), .clk(CLK), .clr(RESET));  // open: count, carry, up
  Stack_Pointer stack_pointer_1 (
    .Data_OUT(stack_pointer_1_data_out), .Load_Data(decoder_1_out4), .Data_IN(multiplexer_1_out),
    .Enable(one_bit_narrow_or_1_o), .CLK(CLK), .Up_Down(not_1_out), .RESET(RESET), .POP(POP));
  Register #(.width(16)) Base_Pointer (
    .D(multiplexer_1_out), .en(decoder_1_out5), .Q(Base_Pointer_q), .clk(CLK), .clr(RESET));
  and and_3 (and_3_out, Word_Select, Reg_Out_Select[2]);
  Multiplexer #(.select(3), .width(16)) multiplexer_2 (
    .in4(stack_pointer_1_data_out), .in5(Base_Pointer_q), .in6(out_18), .out(multiplexer_2_out),
    .sel(Reg_Out_Select), .en(and_2_out));  // open: in0, in1, in2, in3, in7
  Multiplexer #(.enable("false"), .width(16)) multiplexer_3 (
    .in0(Base_Pointer_q), .in1(From_Internal_Data_Bus), .out(multiplexer_3_out),
    .sel(Immediate_Address_Enable));
  Pull_Resistor pull_resistor_1 (.node(multiplexer_2_out));
  Demultiplexer #(.enable("false"), .width(16)) demultiplexer_1 (
    .out0(demultiplexer_1_out0), .out1(To_Main_Bus), .in(multiplexer_2_out), .sel(REG_Out_to_Mainbus_Select));
  Multiplexer #(.enable("false"), .width(16)) multiplexer_4 (
    .in0(multiplexer_3_out), .in1(stack_pointer_1_data_out), .out(To_Adress_Bus), .sel(Cache_Select));
  One_Bit_Narrow_AND one_bit_narrow_and_1 (.O(one_bit_narrow_and_1_o), .A(and_2_out), .B(and_3_out));
  Multiplexer #(.select(2), .width(16)) multiplexer_5 (
    .in0(stack_pointer_1_data_out), .in1(Base_Pointer_q), .in2(out_18), .out(multiplexer_5_out),
    .sel(REG_A_Select[1:0]), .en(REG_A_Select[2]));  // open: in3
  Multiplexer #(.select(2), .width(16)) multiplexer_6 (
    .in0(stack_pointer_1_data_out), .in1(Base_Pointer_q), .in2(out_18), .out(multiplexer_6_out),
    .sel(REG_B_Select[1:0]), .en(REG_B_Select[2]));  // open: in3
  assign To_Internal_Data_Bus = one_bit_narrow_and_1_o ? demultiplexer_1_out0 : 16'bz;  // Controlled_Buffer controlled_buffer_1
  assign A_Out = REG_A_Select[2] ? multiplexer_5_out : 16'bz;  // Controlled_Buffer controlled_buffer_2
  assign B_Out = REG_B_Select[2] ? multiplexer_6_out : 16'bz;  // Controlled_Buffer controlled_buffer_3
endmodule

module General_Purpose_Registers (
  input  Cache_Select,
  input  [1:0] Register_in_Select,
  input  [15:0] From_Main_Bus,
  input  Reg_Out_Enable,
  input  [15:0] From_Internal_Data_Bus,
  input  [2:0] Reg_Out_Select,
  input  [2:0] REG_A_Select,
  input  Reset,
  input  [2:0] REG_B_Select,
  input  CLK,
  input  [2:0] REG_Select,
  input  REG_Out_to_Mainbus_Select,
  input  Word_Select,
  input  REG_Enable,
  output [15:0] To_Internal_Data_Bus,
  output [15:0] To_Main_Bus,
  output [15:0] A_Out,
  output [15:0] B_Out
);

  wire not_1_out, not_2_out, not_3_out, not_4_out, one_bit_narrow_and_1_o, one_bit_narrow_and_2_o,
       register_enable_logic_1_out_4, register_enable_logic_1_out_5, register_enable_logic_1_out_6,
       register_enable_logic_1_out_7, register_enable_logic_1_out_8, register_enable_logic_1_out_9,
       register_enable_logic_1_out_10, register_enable_logic_1_out_11,
       register_output_logic_1_output_to_internalbus_enable;
  wire [7:0] AH_q, AL_q, BH_q, BL_q, CH_q, CL_q, DH_q, DL_q, multiplexer_1_out;
  wire [15:0] multiplexer_2_out, register_output_logic_1_a_out, register_output_logic_1_b_out,
       register_output_logic_1_out_15;

  Register_Enable_Logic register_enable_logic_1 (
    .out_4(register_enable_logic_1_out_4), .out_5(register_enable_logic_1_out_5),
    .out_6(register_enable_logic_1_out_6), .out_7(register_enable_logic_1_out_7),
    .out_8(register_enable_logic_1_out_8), .out_9(register_enable_logic_1_out_9),
    .out_10(register_enable_logic_1_out_10), .out_11(register_enable_logic_1_out_11),
    .Register_Activation(REG_Enable), .Word_Select(Word_Select), .Register_Select(REG_Select));
  not not_1 (not_1_out, Word_Select);
  Multiplexer #(.enable("false"), .width(8)) multiplexer_1 (
    .in0(multiplexer_2_out[15:8]), .in1(multiplexer_2_out[7:0]), .out(multiplexer_1_out), .sel(not_1_out));
  // Probe on AL_q
  Register AL (.D(multiplexer_2_out[7:0]), .en(register_enable_logic_1_out_4), .Q(AL_q), .clk(CLK), .clr(Reset));
  // Probe on BL_q
  Register BL (.D(multiplexer_2_out[7:0]), .en(register_enable_logic_1_out_5), .Q(BL_q), .clk(CLK), .clr(Reset));
  // Probe on CL_q
  Register CL (.D(multiplexer_2_out[7:0]), .en(register_enable_logic_1_out_6), .Q(CL_q), .clk(CLK), .clr(Reset));
  // Probe on DL_q
  Register DL (.D(multiplexer_2_out[7:0]), .en(register_enable_logic_1_out_7), .Q(DL_q), .clk(CLK), .clr(Reset));
  // Probe on AH_q
  Register AH (.D(multiplexer_1_out), .en(register_enable_logic_1_out_8), .Q(AH_q), .clk(CLK), .clr(Reset));
  // Probe on BH_q
  Register BH (.D(multiplexer_1_out), .en(register_enable_logic_1_out_9), .Q(BH_q), .clk(CLK), .clr(Reset));
  // Probe on CH_q
  Register CH (.D(multiplexer_1_out), .en(register_enable_logic_1_out_10), .Q(CH_q), .clk(CLK), .clr(Reset));
  // Probe on DH_q
  Register DH (.D(multiplexer_1_out), .en(register_enable_logic_1_out_11), .Q(DH_q), .clk(CLK), .clr(Reset));
  Register_Output_Logic register_output_logic_1 (
    .Output_to_Internalbus_enable(register_output_logic_1_output_to_internalbus_enable),
    .out_15(register_output_logic_1_out_15), .A_OUT(register_output_logic_1_a_out),
    .B_OUT(register_output_logic_1_b_out), .Output_Enable(Reg_Out_Enable), .Word_Select(Word_Select),
    .REG_A_Select(REG_A_Select), .REG_B_Select(REG_B_Select), .Register_Select(Reg_Out_Select), .AL(AL_q),
    .BL(BL_q), .CL(CL_q), .DL(DL_q), .AH(AH_q), .BH(BH_q), .CH(CH_q), .DH(DH_q));
  not not_2 (not_2_out, REG_B_Select[2]);
  not not_3 (not_3_out, REG_A_Select[2]);
  Multiplexer #(.enable("false"), .select(2), .width(16)) multiplexer_2 (
    .in0(register_output_logic_1_out_15), .in1(From_Internal_Data_Bus), .in2(From_Main_Bus),
    .out(multiplexer_2_out), .sel(Register_in_Select));  // open: in3
  // Probe on register_output_logic_1_out_15
  One_Bit_Narrow_AND one_bit_narrow_and_1 (
    .O(one_bit_narrow_and_1_o), .A(register_output_logic_1_output_to_internalbus_enable), .B(Reg_Out_Enable));
  assign A_Out = not_3_out ? register_output_logic_1_a_out : 16'bz;  // Controlled_Buffer controlled_buffer_1
  assign B_Out = not_2_out ? register_output_logic_1_b_out : 16'bz;  // Controlled_Buffer controlled_buffer_2
  assign To_Internal_Data_Bus = one_bit_narrow_and_2_o ? register_output_logic_1_out_15 : 16'bz;  // Controlled_Buffer controlled_buffer_3
  One_Bit_Narrow_AND one_bit_narrow_and_2 (.O(one_bit_narrow_and_2_o), .A(one_bit_narrow_and_1_o), .B(not_4_out));
  not not_4 (not_4_out, REG_Out_to_Mainbus_Select);
  assign To_Main_Bus = REG_Out_to_Mainbus_Select ? register_output_logic_1_out_15 : 16'bz;  // Controlled_Buffer controlled_buffer_4
endmodule

module Register_Enable_Logic (
  input  [2:0] Register_Select,
  input  Register_Activation,
  input  Word_Select,
  output out_4,
  output out_5,
  output out_6,
  output out_7,
  output out_8,
  output out_9,
  output out_10,
  output out_11
);

  wire and_1_out, decoder_1_out0, decoder_1_out1, decoder_2_out0, decoder_2_out1, decoder_2_out2,
       decoder_2_out3, decoder_3_out0, decoder_3_out1, decoder_3_out2, decoder_3_out3, nand_1_out, or_1_out,
       or_2_out;

  nand nand_1 (nand_1_out, Word_Select, Register_Select[2]);
  Decoder decoder_1 (.out0(decoder_1_out0), .out1(decoder_1_out1), .sel(Register_Select[2]), .en(Register_Activation));
  and and_1 (and_1_out, Register_Activation, Word_Select);
  Pull_Resistor pull_resistor_1 (.node(out_4));
  assign out_4 = nand_1_out ? decoder_2_out0 : 1'bz;  // Controlled_Buffer controlled_buffer_1
  or or_1 (or_1_out, decoder_1_out0, and_1_out);
  or or_2 (or_2_out, and_1_out, decoder_1_out1);
  Decoder #(.select(2)) decoder_2 (
    .out0(decoder_2_out0), .out1(decoder_2_out1), .out2(decoder_2_out2), .out3(decoder_2_out3),
    .sel(Register_Select[1:0]), .en(or_1_out));
  Decoder #(.select(2)) decoder_3 (
    .out0(decoder_3_out0), .out1(decoder_3_out1), .out2(decoder_3_out2), .out3(decoder_3_out3),
    .sel(Register_Select[1:0]), .en(or_2_out));
  Pull_Resistor pull_resistor_2 (.node(out_5));
  Pull_Resistor pull_resistor_3 (.node(out_6));
  Pull_Resistor pull_resistor_4 (.node(out_7));
  Pull_Resistor pull_resistor_5 (.node(out_8));
  assign out_5 = nand_1_out ? decoder_2_out1 : 1'bz;  // Controlled_Buffer controlled_buffer_2
  assign out_6 = nand_1_out ? decoder_2_out2 : 1'bz;  // Controlled_Buffer controlled_buffer_3
  assign out_7 = nand_1_out ? decoder_2_out3 : 1'bz;  // Controlled_Buffer controlled_buffer_4
  assign out_8 = nand_1_out ? decoder_3_out0 : 1'bz;  // Controlled_Buffer controlled_buffer_5
  Pull_Resistor pull_resistor_6 (.node(out_9));
  Pull_Resistor pull_resistor_7 (.node(out_10));
  Pull_Resistor pull_resistor_8 (.node(out_11));
  assign out_9 = nand_1_out ? decoder_3_out1 : 1'bz;  // Controlled_Buffer controlled_buffer_6
  assign out_10 = nand_1_out ? decoder_3_out2 : 1'bz;  // Controlled_Buffer controlled_buffer_7
  assign out_11 = nand_1_out ? decoder_3_out3 : 1'bz;  // Controlled_Buffer controlled_buffer_8
endmodule

module Register_Output_Logic (
  input  [2:0] REG_A_Select,
  input  [2:0] REG_B_Select,
  input  Output_Enable,
  input  Word_Select,
  input  [2:0] Register_Select,
  input  [7:0] AL,
  input  [7:0] BL,
  input  [7:0] CL,
  input  [7:0] DL,
  input  [7:0] AH,
  input  [7:0] BH,
  input  [7:0] CH,
  input  [7:0] DH,
  output Output_to_Internalbus_enable,
  output [15:0] out_15,
  output [15:0] A_OUT,
  output [15:0] B_OUT
);

  wire one_bit_narrow_and_1_o;
  wire [15:0] gpr_reg_output_logic_3_out_11;

  One_Bit_Narrow_AND one_bit_narrow_and_1 (.O(one_bit_narrow_and_1_o), .A(Register_Select[2]), .B(Word_Select));
  GPR_Reg_Output_Logic gpr_reg_output_logic_1 (
    .out_11(A_OUT), .Word_Select(Word_Select), .Register_Select(REG_A_Select), .AL(AL), .BL(BL), .CL(CL),
    .DL(DL), .AH(AH), .BH(BH), .CH(CH), .DH(DH));
  GPR_Reg_Output_Logic gpr_reg_output_logic_2 (
    .out_11(B_OUT), .Word_Select(Word_Select), .Register_Select(REG_B_Select), .AL(AL), .BL(BL), .CL(CL),
    .DL(DL), .AH(AH), .BH(BH), .CH(CH), .DH(DH));
  GPR_Reg_Output_Logic gpr_reg_output_logic_3 (
    .out_11(gpr_reg_output_logic_3_out_11), .Word_Select(Word_Select), .Register_Select(Register_Select),
    .AL(AL), .BL(BL), .CL(CL), .DL(DL), .AH(AH), .BH(BH), .CH(CH), .DH(DH));
  and and_1 (Output_to_Internalbus_enable, Output_Enable, ~one_bit_narrow_and_1_o);  // AND_Gate
  assign out_15 = Output_to_Internalbus_enable ? gpr_reg_output_logic_3_out_11 : 16'bz;  // Controlled_Buffer controlled_buffer_1
endmodule

module GPR_Reg_Output_Logic (
  input  Word_Select,
  input  [2:0] Register_Select,
  input  [7:0] AL,
  input  [7:0] BL,
  input  [7:0] CL,
  input  [7:0] DL,
  input  [7:0] AH,
  input  [7:0] BH,
  input  [7:0] CH,
  input  [7:0] DH,
  output [15:0] out_11
);

  wire and_1_out, and_2_out, not_1_out, one_bit_narrow_or_1_o, one_bit_narrow_or_2_o, pull_resistor_1_node;
  wire [7:0] multiplexer_2_out, multiplexer_3_out;

  not not_1 (not_1_out, Word_Select);
  Pull_Resistor pull_resistor_1 (.node(pull_resistor_1_node));
  assign pull_resistor_1_node = not_1_out ? Register_Select[2] : 1'bz;  // Controlled_Buffer controlled_buffer_1
  and and_1 (and_1_out, ~Word_Select, ~Register_Select[2]);  // AND_Gate
  and and_2 (and_2_out, ~Word_Select, Register_Select[2]);  // AND_Gate
  One_Bit_Narrow_OR one_bit_narrow_or_1 (.O(one_bit_narrow_or_1_o), .A(Word_Select), .B(and_1_out));
  Multiplexer #(.enable("false"), .width(8)) multiplexer_1 (
    .in0(multiplexer_2_out), .in1(multiplexer_3_out), .out(out_11[7:0]), .sel(pull_resistor_1_node));
  Multiplexer #(.select(2), .width(8)) multiplexer_2 (
    .in0(AL), .in1(BL), .in2(CL), .in3(DL), .out(multiplexer_2_out), .sel(Register_Select[1:0]),
    .en(one_bit_narrow_or_1_o));
  Pull_Resistor pull_resistor_2 (.node(out_11[15:8]));
  assign out_11[15:8] = Word_Select ? multiplexer_3_out : 8'bz;  // Controlled_Buffer controlled_buffer_2
  Multiplexer #(.select(2), .width(8)) multiplexer_3 (
    .in0(AH), .in1(BH), .in2(CH), .in3(DH), .out(multiplexer_3_out), .sel(Register_Select[1:0]),
    .en(one_bit_narrow_or_2_o));
  One_Bit_Narrow_OR one_bit_narrow_or_2 (.O(one_bit_narrow_or_2_o), .A(Word_Select), .B(and_2_out));
endmodule

module Swap_Register_Select (
  input  [2:0] in_1,
  input  [2:0] in_2,
  input  in_3,
  output [2:0] out_4,
  output [2:0] out_5
);

  Multiplexer #(.enable("false"), .width(3)) multiplexer_1 (.in0(in_2), .in1(in_1), .out(out_4), .sel(in_3));
  Multiplexer #(.enable("false"), .width(3)) multiplexer_2 (.in0(in_1), .in1(in_2), .out(out_5), .sel(in_3));
endmodule

module Instruction_Decoder (
  input  [31:0] Instruction_Set,
  output Read_Data_from_Memory,
  output Write_Data_to_Memory,
  output Use_Cache,
  output Word_Select,
  output REG_Enable,
  output [2:0] REG_Select,
  output [1:0] Register_in_Select,
  output Reg_Out_Enable,
  output [2:0] Reg_Out_Select,
  output Cache_Select,
  output REG_Out_to_Mainbus_Select,
  output POP,
  output PUSH,
  output [15:0] To_Internal_Bus,
  output Immediate_Address_Enable,
  output ALU_Enable,
  output [2:0] REG_A_Select,
  output [2:0] REG_B_Select,
  output [1:0] ALU_A_IN_Select,
  output [1:0] ALU_B_IN_Select
);

  wire and_1_out, and_2_out, comparator_1_eq, comparator_2_eq, comparator_3_eq, comparator_4_eq,
       comparator_5_eq, comparator_6_eq, comparator_7_gt, not_1_out, one_bit_narrow_and_1_o;
  wire [2:0] multiplexer_1_out, swap_register_select_1_out_4, swap_register_select_1_out_5;
  wire [15:0] controlled_buffer_16_out;

  Comparator comparator_1 (.a(Instruction_Set[31:24]), .b(8'h1), .eq(comparator_1_eq));  // open: gt, lt
  Comparator comparator_2 (.a(Instruction_Set[31:24]), .b(8'h2), .eq(comparator_2_eq));  // open: gt, lt
  Comparator comparator_3 (.a(Instruction_Set[31:24]), .b(8'h3), .eq(comparator_3_eq));  // open: gt, lt
  Comparator comparator_4 (.a(Instruction_Set[31:24]), .b(8'h4), .eq(comparator_4_eq));  // open: gt, lt
  Comparator comparator_5 (.a(Instruction_Set[31:24]), .b(8'h5), .eq(comparator_5_eq));  // open: gt, lt
  Comparator comparator_6 (.a(Instruction_Set[31:24]), .b(8'h20), .eq(comparator_6_eq));  // open: gt, lt
  One_Bit_Narrow_AND one_bit_narrow_and_1 (.O(one_bit_narrow_and_1_o), .A(comparator_1_eq), .B(Instruction_Set[22]));
  Multiplexer #(.enable("false"), .width(3)) multiplexer_1 (
    .in0(Instruction_Set[18:16]), .in1(Instruction_Set[21:19]), .out(multiplexer_1_out),
    .sel(one_bit_narrow_and_1_o));
  Swap_Register_Select swap_register_select_1 (
    .out_4(swap_register_select_1_out_4), .out_5(swap_register_select_1_out_5),
    .in_1(Instruction_Set[18:16]), .in_2(Instruction_Set[21:19]), .in_3(Instruction_Set[22]));
  Comparator #(.width(16)) comparator_7 (
    .a(Instruction_Set[15:0]), .b({16{1'b0}}), .gt(comparator_7_gt));  // open: eq, lt
  assign REG_Out_to_Mainbus_Select = and_2_out ? comparator_3_eq : 1'bz;  // Controlled_Buffer controlled_buffer_1
  assign Reg_Out_Enable = and_2_out ? comparator_3_eq : 1'bz;  // Controlled_Buffer controlled_buffer_2
  assign Reg_Out_Select = and_2_out ? Instruction_Set[18:16] : 3'bz;  // Controlled_Buffer controlled_buffer_3
  and and_1 (and_1_out, Instruction_Set[22], comparator_3_eq);
  not not_1 (not_1_out, Instruction_Set[22]);
  and and_2 (and_2_out, not_1_out, comparator_3_eq);
  Pull_Resistor pull_resistor_1 (.node(REG_Enable));
  assign REG_Enable = comparator_1_eq ? comparator_1_eq : 1'bz;  // Controlled_Buffer controlled_buffer_4
  Pull_Resistor pull_resistor_2 (.node(REG_Select));
  assign REG_Select = comparator_1_eq ? multiplexer_1_out : 3'bz;  // Controlled_Buffer controlled_buffer_5
  assign To_Internal_Bus = comparator_1_eq ? Instruction_Set[15:0] : 16'bz;  // Controlled_Buffer controlled_buffer_6
  assign Register_in_Select = comparator_1_eq ? 2'b01 : 2'bz;  // Controlled_Buffer controlled_buffer_7
  assign REG_Enable = comparator_2_eq ? comparator_2_eq : 1'bz;  // Controlled_Buffer controlled_buffer_8
  assign Reg_Out_Select = comparator_2_eq ? swap_register_select_1_out_4 : 3'bz;  // Controlled_Buffer controlled_buffer_9
  assign REG_Select = comparator_2_eq ? swap_register_select_1_out_5 : 3'bz;  // Controlled_Buffer controlled_buffer_10
  assign Reg_Out_Enable = comparator_2_eq ? comparator_2_eq : 1'bz;  // Controlled_Buffer controlled_buffer_11
  assign Register_in_Select = comparator_2_eq ? 2'b01 : 2'bz;  // Controlled_Buffer controlled_buffer_12
  assign REG_Select = and_1_out ? Instruction_Set[18:16] : 3'bz;  // Controlled_Buffer controlled_buffer_13
  assign REG_Enable = and_1_out ? comparator_3_eq : 1'bz;  // Controlled_Buffer controlled_buffer_14
  assign Register_in_Select = and_1_out ? 2'b10 : 2'bz;  // Controlled_Buffer controlled_buffer_15
  assign controlled_buffer_16_out = comparator_7_gt ? Instruction_Set[15:0] : 16'bz;  // Controlled_Buffer controlled_buffer_16
  assign To_Internal_Bus = comparator_3_eq ? controlled_buffer_16_out : 16'bz;  // Controlled_Buffer controlled_buffer_17
  assign Immediate_Address_Enable = comparator_3_eq ? comparator_7_gt : 1'bz;  // Controlled_Buffer controlled_buffer_18
  assign Read_Data_from_Memory = comparator_3_eq ? and_1_out : 1'bz;  // Controlled_Buffer controlled_buffer_19
  assign Write_Data_to_Memory = comparator_3_eq ? and_2_out : 1'bz;  // Controlled_Buffer controlled_buffer_20
  assign Write_Data_to_Memory = comparator_4_eq ? comparator_4_eq : 1'bz;  // Controlled_Buffer controlled_buffer_21
  assign Use_Cache = comparator_4_eq ? comparator_4_eq : 1'bz;  // Controlled_Buffer controlled_buffer_22
  assign Cache_Select = comparator_4_eq ? comparator_4_eq : 1'bz;  // Controlled_Buffer controlled_buffer_23
  assign PUSH = comparator_4_eq ? comparator_4_eq : 1'bz;  // Controlled_Buffer controlled_buffer_24
  assign Reg_Out_Enable = comparator_4_eq ? comparator_4_eq : 1'bz;  // Controlled_Buffer controlled_buffer_25
  assign Reg_Out_Select = comparator_4_eq ? Instruction_Set[18:16] : 3'bz;  // Controlled_Buffer controlled_buffer_26
  assign REG_Out_to_Mainbus_Select = comparator_4_eq ? comparator_4_eq : 1'bz;  // Controlled_Buffer controlled_buffer_27
  assign Read_Data_from_Memory = comparator_5_eq ? comparator_5_eq : 1'bz;  // Controlled_Buffer controlled_buffer_28
  assign Use_Cache = comparator_5_eq ? comparator_5_eq : 1'bz;  // Controlled_Buffer controlled_buffer_29
  assign Cache_Select = comparator_5_eq ? comparator_5_eq : 1'bz;  // Controlled_Buffer controlled_buffer_30
  assign POP = comparator_5_eq ? comparator_5_eq : 1'bz;  // Controlled_Buffer controlled_buffer_31
  assign REG_Enable = comparator_5_eq ? comparator_5_eq : 1'bz;  // Controlled_Buffer controlled_buffer_32
  assign REG_Select = comparator_5_eq ? Instruction_Set[18:16] : 3'bz;  // Controlled_Buffer controlled_buffer_33
  assign Register_in_Select = comparator_5_eq ? 2'b10 : 2'bz;  // Controlled_Buffer controlled_buffer_34
  assign ALU_Enable = comparator_6_eq ? comparator_6_eq : 1'bz;  // Controlled_Buffer controlled_buffer_35
  assign REG_A_Select = comparator_6_eq ? Instruction_Set[18:16] : 3'bz;  // Controlled_Buffer controlled_buffer_36
  assign REG_Select = comparator_6_eq ? Instruction_Set[18:16] : 3'bz;  // Controlled_Buffer controlled_buffer_37
  assign ALU_A_IN_Select = comparator_6_eq ? 2'b00 : 2'bz;  // Controlled_Buffer controlled_buffer_38
  assign ALU_B_IN_Select = comparator_6_eq ? 2'b11 : 2'bz;  // Controlled_Buffer controlled_buffer_39
  assign Register_in_Select = comparator_6_eq ? 2'b01 : 2'bz;  // Controlled_Buffer controlled_buffer_40
  assign REG_Enable = comparator_6_eq ? comparator_6_eq : 1'bz;  // Controlled_Buffer controlled_buffer_41
  Pull_Resistor pull_resistor_3 (.node(Read_Data_from_Memory));
  Pull_Resistor pull_resistor_4 (.node(Write_Data_to_Memory));
  Pull_Resistor pull_resistor_5 (.node(Use_Cache));
  Pull_Resistor pull_resistor_6 (.node(Register_in_Select));
  Pull_Resistor pull_resistor_7 (.node(Reg_Out_Enable));
  Pull_Resistor pull_resistor_8 (.node(Reg_Out_Select));
  Pull_Resistor pull_resistor_9 (.node(Cache_Select));
  Pull_Resistor pull_resistor_10 (.node(REG_Out_to_Mainbus_Select));
  Pull_Resistor pull_resistor_11 (.node(POP));
  Pull_Resistor pull_resistor_12 (.node(PUSH));
  Pull_Resistor pull_resistor_13 (.node(Immediate_Address_Enable));
  Pull_Resistor pull_resistor_14 (.node(ALU_Enable));
  Pull_Resistor pull_resistor_15 (.node(REG_A_Select));
  Pull_Resistor pull_resistor_16 (.node(REG_B_Select));
  Pull_Resistor pull_resistor_17 (.node(ALU_A_IN_Select));
  Pull_Resistor pull_resistor_18 (.node(ALU_B_IN_Select));

  assign Word_Select = Instruction_Set[23];

  // Notes on the sheet:
  //   INO
  //   MOV
  //   LOD/STO
  //   PUSH
  //   POP
  //   ADD Immediate
endmodule

module One_Bit_Narrow_AND (
  input  A,
  input  B,
  output O
);

  and and_1 (O, A, B);
endmodule

module One_Bit_Narrow_OR (
  input  A,
  input  B,
  output O
);

  or or_1 (O, A, B);
endmodule

module Stack_Pointer (
  input  Up_Down,
  input  Load_Data,
  input  [15:0] Data_IN,
  input  Enable,
  input  POP,
  input  CLK,
  input  RESET,
  output [15:0] Data_OUT
);

  wire [15:0] Stack_Pointer_q, subtractor_1_out;

  Counter #(.max('hffff), .trigger("falling"), .width(16)) Stack_Pointer (
    .load(Load_Data), .D(Data_IN), .count(Enable), .Q(Stack_Pointer_q), .up(Up_Down), .clk(CLK), .clr(RESET));  // open: carry
  Subtractor #(.width(16)) subtractor_1 (.a(Stack_Pointer_q), .b(16'h1), .out(subtractor_1_out));  // open: bin, bout
  Multiplexer #(.enable("false"), .width(16)) multiplexer_1 (
    .in0(Stack_Pointer_q), .in1(subtractor_1_out), .out(Data_OUT), .sel(POP));
endmodule

module ALU (
  input  [15:0] From_Internal_Bus,
  input  [15:0] A_IN,
  input  [15:0] B_IN,
  input  [1:0] ALU_A_IN_Select,
  input  [1:0] ALU_B_IN_Select,
  input  ALU_Select,
  input  [31:0] Instruction_Set,
  input  CLK,
  output [15:0] To_Internal_Bus
);

  wire adder_1_cout, comparator_1_eq;
  wire [0:0] pull_resistor_1_node;
  wire [15:0] adder_1_out, controlled_buffer_2_out, multiplexer_1_out, multiplexer_2_out, or_1_out, or_2_out,
       register_1_q;

  Comparator comparator_1 (.a(Instruction_Set[31:24]), .b(8'h20), .eq(comparator_1_eq));  // open: gt, lt
  Multiplexer #(.enable("false"), .select(2), .width(16)) multiplexer_1 (
    .in0(A_IN), .in1(From_Internal_Bus), .in3(Instruction_Set[15:0]), .out(multiplexer_1_out),
    .sel(ALU_A_IN_Select));  // open: in2
  Multiplexer #(.enable("false"), .select(2), .width(16)) multiplexer_2 (
    .in0(B_IN), .in1(From_Internal_Bus), .in3(Instruction_Set[15:0]), .out(multiplexer_2_out),
    .sel(ALU_B_IN_Select));  // open: in2
  Adder #(.width(16)) adder_1 (
    .a(multiplexer_1_out), .b(multiplexer_2_out), .out(adder_1_out), .cout(adder_1_cout));  // open: cin
  assign To_Internal_Bus = ALU_Select ? or_1_out : 16'bz;  // Controlled_Buffer controlled_buffer_1
  assign or_1_out = controlled_buffer_2_out;  // OR_Gate or_1, 16 bits wide OR_Gate
  assign controlled_buffer_2_out = comparator_1_eq ? adder_1_out : 16'bz;  // Controlled_Buffer controlled_buffer_2
  Pull_Resistor pull_resistor_1 (.node(pull_resistor_1_node[0]));
  assign pull_resistor_1_node[0] = comparator_1_eq ? adder_1_cout : 1'bz;  // Controlled_Buffer controlled_buffer_3
  // Probe on register_1_q
  assign or_2_out = register_1_q | {{15{1'b0}}, pull_resistor_1_node[0]};  // OR_Gate or_2, 16 bits wide
  Register #(.width(16)) register_1 (.D(or_2_out), .Q(register_1_q), .clk(CLK));  // open: en, clr
endmodule
